// Logisim project Tennis.circ as structural Verilog: 12 circuits, main circuit main
module main (
);

  wire button_1_out, cdm_8_mark5_1_p2, cdm_8_mark5_1_p3, clk, comparator_1_eq, comparator_2_eq,
       comparator_3_eq, not_1_out;
  wire [3:0] digits_1_bus_0_2, digits_1_bus_0_3, digits_2_bus_0_2, digits_2_bus_0_3;
  wire [4:0] joystick_1_y, kinematiccontroller2_1_ballx, kinematiccontroller2_1_bally,
       kinematiccontroller2_1_chipid, kinematiccontroller2_1_leftyout, kinematiccontroller2_1_rightyout,
       not_2_out, videosection_1_ballx_2, videosection_1_bally_2, videosection_1_chipid_2,
       videosection_1_leftbaty_2, videosection_1_rightbaty_2, videosection_2_ballx_2, videosection_2_bally_2,
       videosection_2_chipid_2, videosection_2_leftbaty_2, videosection_2_rightbaty_2,
       videosection_3_ballx_2, videosection_3_bally_2, videosection_3_chipid_2, videosection_3_leftbaty_2,
       videosection_3_rightbaty_2;
  wire [7:0] addr, cdm_8_mark5_1_p5, cdm_8_mark5_1_p6, controlled_buffer_1_out, kinematiccontroller2_1_vxy,
       kinematiccontroller2_1_xball, kinematiccontroller2_1_yball, ls, rs;
  wire [31:0] videosection_1__0, videosection_1_out_7, videosection_1_out_8, videosection_1_out_9,
       videosection_1_out_10, videosection_1_out_11, videosection_1_out_12, videosection_1_out_13,
       videosection_2__0, videosection_2_out_7, videosection_2_out_8, videosection_2_out_9,
       videosection_2_out_10, videosection_2_out_11, videosection_2_out_12, videosection_2_out_13,
       videosection_3__0, videosection_3_out_7, videosection_3_out_8, videosection_3_out_9,
       videosection_3_out_10, videosection_3_out_11, videosection_3_out_12, videosection_3_out_13,
       videosection_4__0, videosection_4_out_7, videosection_4_out_8, videosection_4_out_9,
       videosection_4_out_10, videosection_4_out_11, videosection_4_out_12, videosection_4_out_13;

  // CdM_8_mark5 cdm_8_mark5_1: pin names not known; wires that end beside it: clk, cdm_8_mark5_1_p2, cdm_8_mark5_1_p3, addr, cdm_8_mark5_1_p5, cdm_8_mark5_1_p6
  not not_1 (not_1_out, cdm_8_mark5_1_p3);
  assign controlled_buffer_1_out = not_1_out ? cdm_8_mark5_1_p5 : 8'bz;  // Controlled_Buffer controlled_buffer_1
  assign cdm_8_mark5_1_p6 = cdm_8_mark5_1_p3 ? controlled_buffer_1_out : 8'bz;  // Controlled_Buffer controlled_buffer_2
  RAM ram_1 (
    .addr(addr), .data(controlled_buffer_1_out), .sel(cdm_8_mark5_1_p2), .ld(cdm_8_mark5_1_p3));  // open: clk, clr
  ROM rom_1 (.addr(addr), .data(controlled_buffer_1_out));  // open: sel
  Comparator comparator_1 (.a(addr), .b(8'h80), .eq(comparator_1_eq));  // open: gt, lt
  assign controlled_buffer_1_out = comparator_1_eq ? kinematiccontroller2_1_vxy : 8'bz;  // Controlled_Buffer controlled_buffer_3
  Comparator comparator_2 (.a(addr), .b(8'h80), .eq(comparator_2_eq));  // open: gt, lt
  Comparator comparator_3 (.a(addr), .b(8'h80), .eq(comparator_3_eq));  // open: gt, lt
  assign controlled_buffer_1_out = comparator_2_eq ? kinematiccontroller2_1_xball : 8'bz;  // Controlled_Buffer controlled_buffer_4
  assign controlled_buffer_1_out = comparator_3_eq ? kinematiccontroller2_1_yball : 8'bz;  // Controlled_Buffer controlled_buffer_5
  Hex_Digit_Display hex_digit_display_1 (.value(digits_1_bus_0_2));  // open: dp
  digits digits_1 (.bus_0_2(digits_1_bus_0_2), .bus_0_3(digits_1_bus_0_3), .bus_0(ls));
  Joystick #(.bits(5)) joystick_1 (.y(joystick_1_y));  // open: x
  Button button_1 (.out(button_1_out));
  Hex_Digit_Display hex_digit_display_2 (.value(digits_1_bus_0_3));  // open: dp
  assign not_2_out = ~joystick_1_y;  // NOT_Gate not_2, 5 bits wide
  DotMatrix #(.matrixcols(32), .matrixrows(32)) dotmatrix_1 (
    .col0(videosection_1__0), .col1(videosection_1_out_7), .col2(videosection_1_out_8),
    .col3(videosection_1_out_9), .col4(videosection_1_out_10), .col5(videosection_1_out_11),
    .col6(videosection_1_out_12), .col7(videosection_1_out_13), .col8(videosection_2__0),
    .col9(videosection_2_out_7), .col10(videosection_2_out_8), .col11(videosection_2_out_9),
    .col12(videosection_2_out_10), .col13(videosection_2_out_11), .col14(videosection_2_out_12),
    .col15(videosection_2_out_13), .col16(videosection_3__0), .col17(videosection_3_out_7),
    .col18(videosection_3_out_8), .col19(videosection_3_out_9), .col20(videosection_3_out_10),
    .col21(videosection_3_out_11), .col22(videosection_3_out_12), .col23(videosection_3_out_13),
    .col24(videosection_4__0), .col25(videosection_4_out_7), .col26(videosection_4_out_8),
    .col27(videosection_4_out_9), .col28(videosection_4_out_10), .col29(videosection_4_out_11),
    .col30(videosection_4_out_12), .col31(videosection_4_out_13));
  kinematicController2 kinematiccontroller2_1 (
    .xball(kinematiccontroller2_1_xball), .yball(kinematiccontroller2_1_yball),
    .vxy(kinematiccontroller2_1_vxy), .reset(button_1_out), .leftYIn(not_2_out), .scoreA(ls), .clock(clk),
    .scoreB(rs), .chipId(kinematiccontroller2_1_chipid), .ballX(kinematiccontroller2_1_ballx),
    .ballY(kinematiccontroller2_1_bally), .leftYout(kinematiccontroller2_1_leftyout),
    .rightYout(kinematiccontroller2_1_rightyout));  // open: RightYIn
  videoSection videosection_1 (
    .chipId(kinematiccontroller2_1_chipid), .ballX(kinematiccontroller2_1_ballx),
    .ballY(kinematiccontroller2_1_bally), .leftBatY(kinematiccontroller2_1_leftyout),
    .rightBatY(kinematiccontroller2_1_rightyout), .chipId_2(videosection_1_chipid_2),
    .ballX_2(videosection_1_ballx_2), .ballY_2(videosection_1_bally_2),
    .leftBatY_2(videosection_1_leftbaty_2), .rightBatY_2(videosection_1_rightbaty_2), ._0(videosection_1__0),
    .out_7(videosection_1_out_7), .out_8(videosection_1_out_8), .out_9(videosection_1_out_9),
    .out_10(videosection_1_out_10), .out_11(videosection_1_out_11), .out_12(videosection_1_out_12),
    .out_13(videosection_1_out_13));
  Clock clock_1 (.out(clk));
  videoSection videosection_2 (
    .chipId(videosection_1_chipid_2), .ballX(videosection_1_ballx_2), .ballY(videosection_1_bally_2),
    .leftBatY(videosection_1_leftbaty_2), .rightBatY(videosection_1_rightbaty_2),
    .chipId_2(videosection_2_chipid_2), .ballX_2(videosection_2_ballx_2), .ballY_2(videosection_2_bally_2),
    .leftBatY_2(videosection_2_leftbaty_2), .rightBatY_2(videosection_2_rightbaty_2), ._0(videosection_2__0),
    .out_7(videosection_2_out_7), .out_8(videosection_2_out_8), .out_9(videosection_2_out_9),
    .out_10(videosection_2_out_10), .out_11(videosection_2_out_11), .out_12(videosection_2_out_12),
    .out_13(videosection_2_out_13));
  videoSection videosection_3 (
    .chipId(videosection_2_chipid_2), .ballX(videosection_2_ballx_2), .ballY(videosection_2_bally_2),
    .leftBatY(videosection_2_leftbaty_2), .rightBatY(videosection_2_rightbaty_2),
    .chipId_2(videosection_3_chipid_2), .ballX_2(videosection_3_ballx_2), .ballY_2(videosection_3_bally_2),
    .leftBatY_2(videosection_3_leftbaty_2), .rightBatY_2(videosection_3_rightbaty_2), ._0(videosection_3__0),
    .out_7(videosection_3_out_7), .out_8(videosection_3_out_8), .out_9(videosection_3_out_9),
    .out_10(videosection_3_out_10), .out_11(videosection_3_out_11), .out_12(videosection_3_out_12),
    .out_13(videosection_3_out_13));
  videoSection videosection_4 (
    .chipId(videosection_3_chipid_2), .ballX(videosection_3_ballx_2), .ballY(videosection_3_bally_2),
    .leftBatY(videosection_3_leftbaty_2), .rightBatY(videosection_3_rightbaty_2), ._0(videosection_4__0),
    .out_7(videosection_4_out_7), .out_8(videosection_4_out_8), .out_9(videosection_4_out_9),
    .out_10(videosection_4_out_10), .out_11(videosection_4_out_11), .out_12(videosection_4_out_12),
    .out_13(videosection_4_out_13));  // open: chipId_2, ballX_2, ballY_2, leftBatY_2, rightBatY_2
  Hex_Digit_Display hex_digit_display_3 (.value(digits_2_bus_0_2));  // open: dp
  digits digits_2 (.bus_0_2(digits_2_bus_0_2), .bus_0_3(digits_2_bus_0_3), .bus_0(rs));
  Hex_Digit_Display hex_digit_display_4 (.value(digits_2_bus_0_3));  // open: dp
endmodule

module VideoChip (
  input  [4:0] chipId,
  input  [4:0] ballX,
  input  [4:0] ballY,
  input  [4:0] leftBatY,
  input  [4:0] rightBatY,
  output [31:0] bitPattern,
  output [4:0] chipId_2,
  output [4:0] ballX_2,
  output [4:0] ballY_2,
  output [4:0] leftBatY_2,
  output [4:0] rightBatY_2
);

  wire \and , and2, and_1_out, and_2_out, and_5_out, comparator_1_eq, comparator_2_eq, comparator_3_eq,
       not_1_out, not_2_out, not_3_out, not_4_out, not_5_out, or_1_out;
  wire [31:0] adder_1_out, adder_2_out, ballvideo_1_out, chip_1_out_2, rightBatY_t;

  chip chip_1 (.in_1(leftBatY), .out_2(chip_1_out_2));
  Comparator #(.width(5), .mode("unsigned")) comparator_1 (
    .a(chipId), .b(5'b00011), .eq(comparator_1_eq));  // open: gt, lt
  Comparator #(.width(5), .mode("unsigned")) comparator_2 (
    .a(chipId), .b(5'b11100), .eq(comparator_2_eq));  // open: gt, lt
  Comparator #(.width(5), .mode("unsigned")) comparator_3 (
    .a(chipId), .b(ballX), .eq(comparator_3_eq));  // open: gt, lt
  ballVideo ballvideo_1 (.in(ballY), .out(ballvideo_1_out));
  Multiplexer #(.width(32)) multiplexer_1 (.in1(chip_1_out_2), .out(bitPattern), .sel(and_1_out));  // open: in0, en
  and and_1 (and_1_out, comparator_1_eq, not_2_out, not_1_out);
  not not_1 (not_1_out, \and );
  not not_2 (not_2_out, and2);
  or or_1 (or_1_out, comparator_1_eq, comparator_2_eq, comparator_3_eq);
  Multiplexer #(.width(32)) multiplexer_2 (.in1(ballvideo_1_out), .out(bitPattern), .sel(and_2_out));  // open: in0, en
  and and_2 (and_2_out, comparator_3_eq, not_4_out, not_3_out);
  not not_3 (not_3_out, \and );
  Adder #(.width(32)) adder_1 (.a(chip_1_out_2), .b(ballvideo_1_out), .out(adder_1_out));  // open: cin, cout
  not not_4 (not_4_out, and2);
  chip chip_2 (.in_1(rightBatY), .out_2(rightBatY_t));
  Multiplexer #(.width(32)) multiplexer_3 (.in0({32{1'b0}}), .out(bitPattern), .sel(or_1_out));  // open: in1, en
  Multiplexer #(.width(32)) multiplexer_4 (.in1(rightBatY_t), .out(bitPattern), .sel(and_5_out));  // open: in0, en
  and and_3 (and2, comparator_3_eq, comparator_2_eq);
  Multiplexer #(.width(32)) multiplexer_5 (.in1(adder_1_out), .out(bitPattern), .sel(\and ));  // open: in0, en
  and and_4 (\and , comparator_1_eq, comparator_3_eq);
  and and_5 (and_5_out, comparator_2_eq, not_5_out);
  Adder #(.width(32)) adder_2 (.a(ballvideo_1_out), .b(rightBatY_t), .out(adder_2_out));  // open: cin, cout
  inc inc_1 (.X(chipId), .R(chipId_2));  // open: Cout
  not not_5 (not_5_out, and2);
  Multiplexer #(.width(32)) multiplexer_6 (.in1(adder_2_out), .out(bitPattern), .sel(and2));  // open: in0, en

  assign ballX_2 = ballX;
  assign ballY_2 = ballY;
  assign leftBatY_2 = leftBatY;
  assign rightBatY_2 = rightBatY;
endmodule

module videoSection (
  input  [4:0] chipId,
  input  [4:0] ballX,
  input  [4:0] ballY,
  input  [4:0] leftBatY,
  input  [4:0] rightBatY,
  output [31:0] _0,
  output [31:0] out_7,
  output [31:0] out_8,
  output [31:0] out_9,
  output [31:0] out_10,
  output [31:0] out_11,
  output [31:0] out_12,
  output [31:0] out_13,
  output [4:0] chipId_2,
  output [4:0] ballX_2,
  output [4:0] ballY_2,
  output [4:0] leftBatY_2,
  output [4:0] rightBatY_2
);

  wire [4:0] videochip_1_ballx_2, videochip_1_bally_2, videochip_1_chipid_2, videochip_1_leftbaty_2,
       videochip_1_rightbaty_2, videochip_2_ballx_2, videochip_2_bally_2, videochip_2_chipid_2,
       videochip_2_leftbaty_2, videochip_2_rightbaty_2, videochip_3_ballx_2, videochip_3_bally_2,
       videochip_3_chipid_2, videochip_3_leftbaty_2, videochip_3_rightbaty_2, videochip_4_ballx_2,
       videochip_4_bally_2, videochip_4_chipid_2, videochip_4_leftbaty_2, videochip_4_rightbaty_2,
       videochip_5_ballx_2, videochip_5_bally_2, videochip_5_chipid_2, videochip_5_leftbaty_2,
       videochip_5_rightbaty_2, videochip_6_ballx_2, videochip_6_bally_2, videochip_6_chipid_2,
       videochip_6_leftbaty_2, videochip_6_rightbaty_2, videochip_8_ballx_2, videochip_8_bally_2,
       videochip_8_chipid_2, videochip_8_leftbaty_2, videochip_8_rightbaty_2;

  VideoChip videochip_1 (
    .chipId(chipId), .ballX(ballX), .ballY(ballY), .leftBatY(leftBatY), .rightBatY(rightBatY),
    .bitPattern(_0), .chipId_2(videochip_1_chipid_2), .ballX_2(videochip_1_ballx_2),
    .ballY_2(videochip_1_bally_2), .leftBatY_2(videochip_1_leftbaty_2), .rightBatY_2(videochip_1_rightbaty_2));
  VideoChip videochip_2 (
    .chipId(videochip_3_chipid_2), .ballX(videochip_3_ballx_2), .ballY(videochip_3_bally_2),
    .leftBatY(videochip_3_leftbaty_2), .rightBatY(videochip_3_rightbaty_2), .bitPattern(out_8),
    .chipId_2(videochip_2_chipid_2), .ballX_2(videochip_2_ballx_2), .ballY_2(videochip_2_bally_2),
    .leftBatY_2(videochip_2_leftbaty_2), .rightBatY_2(videochip_2_rightbaty_2));
  VideoChip videochip_3 (
    .chipId(videochip_1_chipid_2), .ballX(videochip_1_ballx_2), .ballY(videochip_1_bally_2),
    .leftBatY(videochip_1_leftbaty_2), .rightBatY(videochip_1_rightbaty_2), .bitPattern(out_7),
    .chipId_2(videochip_3_chipid_2), .ballX_2(videochip_3_ballx_2), .ballY_2(videochip_3_bally_2),
    .leftBatY_2(videochip_3_leftbaty_2), .rightBatY_2(videochip_3_rightbaty_2));
  VideoChip videochip_4 (
    .chipId(videochip_6_chipid_2), .ballX(videochip_6_ballx_2), .ballY(videochip_6_bally_2),
    .leftBatY(videochip_6_leftbaty_2), .rightBatY(videochip_6_rightbaty_2), .bitPattern(out_11),
    .chipId_2(videochip_4_chipid_2), .ballX_2(videochip_4_ballx_2), .ballY_2(videochip_4_bally_2),
    .leftBatY_2(videochip_4_leftbaty_2), .rightBatY_2(videochip_4_rightbaty_2));
  VideoChip videochip_5 (
    .chipId(videochip_2_chipid_2), .ballX(videochip_2_ballx_2), .ballY(videochip_2_bally_2),
    .leftBatY(videochip_2_leftbaty_2), .rightBatY(videochip_2_rightbaty_2), .bitPattern(out_9),
    .chipId_2(videochip_5_chipid_2), .ballX_2(videochip_5_ballx_2), .ballY_2(videochip_5_bally_2),
    .leftBatY_2(videochip_5_leftbaty_2), .rightBatY_2(videochip_5_rightbaty_2));
  VideoChip videochip_6 (
    .chipId(videochip_5_chipid_2), .ballX(videochip_5_ballx_2), .ballY(videochip_5_bally_2),
    .leftBatY(videochip_5_leftbaty_2), .rightBatY(videochip_5_rightbaty_2), .bitPattern(out_10),
    .chipId_2(videochip_6_chipid_2), .ballX_2(videochip_6_ballx_2), .ballY_2(videochip_6_bally_2),
    .leftBatY_2(videochip_6_leftbaty_2), .rightBatY_2(videochip_6_rightbaty_2));
  VideoChip videochip_7 (
    .chipId(videochip_8_chipid_2), .ballX(videochip_8_ballx_2), .ballY(videochip_8_bally_2),
    .leftBatY(videochip_8_leftbaty_2), .rightBatY(videochip_8_rightbaty_2), .bitPattern(out_13),
    .chipId_2(chipId_2), .ballX_2(ballX_2), .ballY_2(ballY_2), .leftBatY_2(leftBatY_2),
    .rightBatY_2(rightBatY_2));
  VideoChip videochip_8 (
    .chipId(videochip_4_chipid_2), .ballX(videochip_4_ballx_2), .ballY(videochip_4_bally_2),
    .leftBatY(videochip_4_leftbaty_2), .rightBatY(videochip_4_rightbaty_2), .bitPattern(out_12),
    .chipId_2(videochip_8_chipid_2), .ballX_2(videochip_8_ballx_2), .ballY_2(videochip_8_bally_2),
    .leftBatY_2(videochip_8_leftbaty_2), .rightBatY_2(videochip_8_rightbaty_2));
endmodule

module kinematicController (
  input  reset,
  input  [4:0] Joystick,
  input  [4:0] rightBatPositionIn,
  input  Clock,
  output [7:0] scoreA,
  output [7:0] scoreB,
  output [7:0] xball,
  output [4:0] chipId,
  output [7:0] yball,
  output [4:0] ballX,
  output [4:0] ballY,
  output [4:0] leftBatY,
  output [4:0] rightBatY,
  output [7:0] vxy
);

  wire adder_3_cout, adder_4_cout, adder_7_cout, adder_8_cout, and_1_out, and_2_out, and_3_out, BContact,
       comparator_2_eq, comparator_3_eq, comparator_4_eq, comparator_5_eq, comparator_6_eq, comparator_7_eq,
       enableComponentX, enableComponentY, hitA, hitB, inrange_1_showarow, inrange_2_showarow, not_1_out,
       not_3_out, not_4_out, or_1_out, or_2_out, yreg;
  wire [2:0] ballX_q, ballY_q, multiplexer_3_out, multiplexer_4_out, reflect_1_output, reflect_2_output;
  wire [4:0] multiplexer_5_out;
  wire [7:0] adder_1_out, adder_2_out, adder_5_out, adder_6_out, multiplexer_1_out, multiplexer_2_out;

  Adder adder_1 (.a({ballX, ballX_q}), .b({ballY, ballY_q}), .out(adder_1_out));  // open: cin, cout
  reflect reflect_1 (.\input (vxy[2:0]), .\output (reflect_1_output));
  reflect reflect_2 (.\input (vxy[5:3]), .\output (reflect_2_output));
  Adder adder_2 (.a({ballY, ballY_q}), .b({{6{vxy[5]}}, vxy[4:3]}), .out(adder_2_out));  // open: cin, cout
  Multiplexer #(.width(8)) multiplexer_1 (
    .in0(adder_2_out), .in1(8'h80), .out(multiplexer_1_out), .sel(reset));  // open: en
  or or_1 (or_1_out, yreg, reset);
  Multiplexer #(.width(8)) multiplexer_2 (
    .in0(adder_1_out), .in1(8'hc0), .out(multiplexer_2_out), .sel(reset));  // open: en
  or or_2 (or_2_out, and_1_out, reset);
  and and_1 (and_1_out, BContact, not_1_out);
  Multiplexer #(.width(3)) multiplexer_3 (
    .in0(reflect_1_output), .in1(3'b110), .out(multiplexer_3_out), .sel(reset));  // open: en
  Register #(.width(3)) componentX (
    .D(multiplexer_3_out), .en(enableComponentX), .Q(vxy[2:0]), .clk(Clock));  // open: clr
  Register #(.width(3)) componentY (
    .D(multiplexer_4_out), .en(enableComponentY), .Q(vxy[5:3]), .clk(Clock));  // open: clr
  Multiplexer #(.width(3)) multiplexer_4 (
    .in0(reflect_2_output), .in1(3'b001), .out(multiplexer_4_out), .sel(reset));  // open: en
  Register #(.trigger("low")) u_ballY (
    .D(multiplexer_1_out), .en(or_1_out), .Q({ballY, ballY_q}), .clk(Clock));  // open: clr
  Register #(.trigger("low")) u_ballX (
    .D(multiplexer_2_out), .en(or_2_out), .Q({ballX, ballX_q}), .clk(Clock));  // open: clr
  Comparator #(.width(5), .mode("unsigned")) comparator_1 (
    .a({ballX[1:0], ballX_q}), .b(5'b01110));  // open: gt, eq, lt
  Adder adder_3 (.a({ballX, ballX_q}), .b({{6{vxy[2]}}, vxy[1:0]}), .cout(adder_3_cout));  // open: out, cin
  Comparator #(.width(1)) comparator_2 (.a(vxy[2]), .b(1'b1), .eq(comparator_2_eq));  // open: gt, lt
  Comparator #(.width(1)) comparator_3 (.a(vxy[5]), .b(1'b1), .eq(comparator_3_eq));  // open: gt, lt
  Multiplexer #(.width(5)) multiplexer_5 (
    .in0(rightBatPositionIn), .in1(5'b01111), .out(multiplexer_5_out), .sel(reset));  // open: en
  Register #(.width(5)) rightBatPosition (
    .D(multiplexer_5_out), .en(ballX[1]), .Q(rightBatY), .clk(Clock));  // open: clr
  Comparator #(.width(1)) comparator_4 (.a(adder_3_cout), .b(comparator_2_eq), .eq(comparator_4_eq));  // open: gt, lt
  not not_1 (not_1_out, comparator_4_eq);
  Adder adder_4 (.a({ballY, ballY_q}), .b({{6{vxy[5]}}, vxy[4:3]}), .cout(adder_4_cout));  // open: out, cin
  Comparator #(.width(1)) comparator_5 (.a(adder_4_cout), .b(comparator_3_eq), .eq(comparator_5_eq));  // open: gt, lt
  Adder adder_5 (.a({ballX, ballX_q}), .b(8'he4), .out(adder_5_out));  // open: cin, cout
  or or_3 (hitB, not_1_out, vxy[2]);
  Adder adder_6 (.a({ballX, ballX_q}), .b(8'h1c), .out(adder_6_out));  // open: cin, cout
  or or_4 (hitA, vxy[5], yreg);
  not not_2 (yreg, comparator_5_eq);
  Adder adder_7 (.a(adder_5_out), .b({{6{vxy[2]}}, vxy[1:0]}), .cout(adder_7_cout));  // open: out, cin
  Adder adder_8 (.a(adder_6_out), .b({{6{vxy[2]}}, vxy[1:0]}), .cout(adder_8_cout));  // open: out, cin
  inrange inrange_1 (.Yball(ballY), .Ybat(Joystick), .ShowArow(inrange_1_showarow));
  not not_3 (not_3_out, comparator_6_eq);
  Comparator #(.width(1)) comparator_6 (.a(adder_7_cout), .b(comparator_2_eq), .eq(comparator_6_eq));  // open: gt, lt
  inrange inrange_2 (.Yball(ballY), .Ybat(rightBatY), .ShowArow(inrange_2_showarow));
  Comparator #(.width(1)) comparator_7 (.a(adder_8_cout), .b(comparator_2_eq), .eq(comparator_7_eq));  // open: gt, lt
  not not_4 (not_4_out, comparator_7_eq);
  Counter scoreLeft (.load(hitA), .count(hitA), .Q(scoreA), .clk(Clock), .clr(reset));  // open: D, carry
  and and_2 (and_2_out, inrange_1_showarow, not_3_out);
  and and_3 (and_3_out, inrange_2_showarow, not_4_out);
  or or_5 (BContact, and_2_out, and_3_out);
  or or_6 (enableComponentY, yreg, reset);
  Counter scoreRight (.load(hitB), .count(hitB), .Q(scoreB), .clk(Clock), .clr(reset));  // open: D, carry
  or or_7 (enableComponentX, reset, BContact, not_1_out);

  assign chipId = {5{1'b0}};
  assign leftBatY = Joystick;
  assign vxy[7:6] = 2'b00;

  // Other names for the same wires on the sheet: longVY[7:0] = {{6{vxy[5]}}, vxy[4:3]}

  // Notes on the sheet:
  //   hitB
  //   hitA
  //   LBcontact
  //   RBcontact
  //   BContact
endmodule

module inc (
  input  [4:0] X,
  output [4:0] R,
  output Cout
);

  wire [4:1] and_1_out;

  assign {Cout, and_1_out} = {and_1_out, 1'b1} & X;  // AND_Gate and_1, 5 bits wide
  assign R = X ^ {and_1_out, 1'b1};  // XOR_Gate xor_1, 5 bits wide
endmodule

module ballVideo (
  input  [4:0] in,
  output [31:0] out
);

  Shifter #(.width(32), .shift("rl")) shifter_1 (.in(32'h1), .\dist (in), .out(out));
endmodule

module chip (
  input  [4:0] in_1,
  output [31:0] out_2
);

  wire comparator_1_eq;
  wire [4:0] subtractor_1_out;
  wire [31:0] shifter_1_out, shifter_2_out;

  Comparator #(.width(5), .mode("unsigned")) comparator_1 (
    .a(in_1), .b(5'b11110), .eq(comparator_1_eq));  // open: gt, lt
  Shifter #(.width(32)) shifter_1 (.in(32'h7), .\dist (in_1), .out(shifter_1_out));
  Subtractor #(.width(5)) subtractor_1 (.a(in_1), .b(5'b00001), .out(subtractor_1_out));  // open: bin, bout
  Shifter #(.width(32)) shifter_2 (.in(32'h7), .\dist (subtractor_1_out), .out(shifter_2_out));
  Multiplexer #(.width(32)) multiplexer_1 (
    .in0(shifter_1_out), .in1(shifter_2_out), .out(out_2), .sel(comparator_1_eq));  // open: en
endmodule

module reflect (
  input  [2:0] \input ,
  output [2:0] \output 
);

  wire comparator_1_eq;
  wire [2:0] adder_1_out, not_1_out, not_2_out;

  assign not_1_out = ~\input ;  // NOT_Gate not_1, 3 bits wide
  Adder #(.width(3)) adder_1 (.a(not_1_out), .b(3'b001), .out(adder_1_out));  // open: cin, cout
  assign not_2_out = ~\input ;  // NOT_Gate not_2, 3 bits wide
  Comparator #(.width(3), .mode("unsigned")) comparator_1 (
    .a(\input ), .b(3'b100), .eq(comparator_1_eq));  // open: gt, lt
  Multiplexer #(.width(3)) multiplexer_1 (
    .in0(adder_1_out), .in1(not_2_out), .out(\output ), .sel(comparator_1_eq));  // open: en
endmodule

module inrange (
  input  [4:0] Yball,
  input  [4:0] Ybat,
  output ShowArow
);

  wire comparator_1_eq, comparator_2_eq, comparator_3_eq;
  wire [4:0] adder_1_out, adder_2_out;

  Comparator #(.width(5), .mode("unsigned")) comparator_1 (
    .a(Yball), .b(adder_1_out), .eq(comparator_1_eq));  // open: gt, lt
  Adder #(.width(5)) adder_1 (.a(Ybat), .b(5'b00010), .out(adder_1_out));  // open: cin, cout
  Comparator #(.width(5), .mode("unsigned")) comparator_2 (.a(Yball), .b(Ybat), .eq(comparator_2_eq));  // open: gt, lt
  Comparator #(.width(5), .mode("unsigned")) comparator_3 (
    .a(Yball), .b(adder_2_out), .eq(comparator_3_eq));  // open: gt, lt
  Adder #(.width(5)) adder_2 (.a(5'b00001), .b(Ybat), .out(adder_2_out));  // open: cin, cout
  or or_1 (ShowArow, comparator_1_eq, comparator_2_eq, comparator_3_eq);
endmodule

module digits (
  input  [7:0] bus_0,
  output [3:0] bus_0_2,
  output [3:0] bus_0_3
);


  assign bus_0_2 = bus_0[7:4];
  assign bus_0_3 = bus_0[3:0];
endmodule

module kinematicController2 (
  input  reset,
  input  [4:0] leftYIn,
  input  [4:0] RightYIn,
  input  clock,
  output [4:0] chipId,
  output [4:0] ballX,
  output [7:0] xball,
  output [7:0] yball,
  output [4:0] ballY,
  output [7:0] vxy,
  output [4:0] leftYout,
  output [4:0] rightYout,
  output [7:0] scoreA,
  output [7:0] scoreB
);

  wire adder_4_cout, adder_8_cout, adder_9_cout, adder_10_cout, and_1_out, Bcontact, comparator_1_eq,
       comparator_2_eq, comparator_3_eq, comparator_4_eq, hitA, hitB, inrange_1_showarow, inrange_2_showarow,
       LBcontact, not_1_out, not_2_out, not_3_out, not_4_out, not_5_out, not_6_out, not_9_out, or_1_out,
       or_2_out, or_3_out, or_4_out, RBcontact, xrefl, yrefl;
  wire [2:0] multiplexer_4_out, multiplexer_6_out, reflect_1_output, reflect_2_output;
  wire [4:0] multiplexer_1_out;
  wire [7:0] adder_1_out, adder_2_out, adder_3_out, adder_5_out, adder_6_out, adder_7_out, multiplexer_2_out,
       multiplexer_3_out, scA_q, scB_q;

  Adder adder_1 (.a({{6{vxy[2]}}, vxy[1:0]}), .b({ballX, xball[2:0]}), .out(adder_1_out));  // open: cin, cout
  Multiplexer #(.width(5)) multiplexer_1 (
    .in0(RightYIn), .in1(5'b01111), .out(multiplexer_1_out), .sel(reset));  // open: en
  Multiplexer #(.width(8)) multiplexer_2 (
    .in0(adder_1_out), .in1(8'hc0), .out(multiplexer_2_out), .sel(reset));  // open: en
  or or_1 (or_1_out, and_1_out, reset);
  Adder adder_2 (.a({{6{vxy[5]}}, vxy[4:3]}), .b({ballY, yball[2:0]}), .out(adder_2_out));  // open: cin, cout
  Multiplexer #(.width(8)) multiplexer_3 (
    .in0(adder_2_out), .in1(8'h80), .out(multiplexer_3_out), .sel(reset));  // open: en
  or or_2 (or_2_out, not_4_out, reset);
  Register #(.width(5), .trigger("falling")) rightYreg (
    .D(multiplexer_1_out), .en(not_1_out), .Q(rightYout), .clk(clock));  // open: clr
  not not_1 (not_1_out, ballX[4]);
  Adder adder_3 (.a({ballX, xball[2:0]}), .b(8'he4), .out(adder_3_out));  // open: cin, cout
  Register #(.trigger("falling")) xreg (
    .D(multiplexer_2_out), .en(or_1_out), .Q({ballX, xball[2:0]}), .clk(clock));  // open: clr
  not not_2 (not_2_out, xrefl);
  and and_1 (and_1_out, not_2_out, not_3_out);
  not not_3 (not_3_out, Bcontact);
  Register #(.trigger("falling")) yreg (
    .D(multiplexer_3_out), .en(or_2_out), .Q({ballY, yball[2:0]}), .clk(clock));  // open: clr
  not not_4 (not_4_out, yrefl);
  Adder adder_4 (.a(adder_3_out), .b({{6{vxy[2]}}, vxy[1:0]}), .cout(adder_4_cout));  // open: out, cin
  not not_5 (not_5_out, comparator_1_eq);
  Comparator #(.width(1)) comparator_1 (.a(adder_4_cout), .b(vxy[2]), .eq(comparator_1_eq));  // open: gt, lt
  inrange inrange_1 (.Yball(ballY), .Ybat(leftYIn), .ShowArow(inrange_1_showarow));
  reflect reflect_1 (.\input (vxy[2:0]), .\output (reflect_1_output));
  and and_2 (LBcontact, not_5_out, inrange_1_showarow);
  Multiplexer #(.width(3)) multiplexer_4 (
    .in0(reflect_1_output), .in1(3'b110), .out(multiplexer_4_out), .sel(reset));  // open: en
  or or_3 (or_3_out, reset, Bcontact, xrefl);
  Register scA (.D(scoreA), .en(hitB), .Q(scA_q), .clk(clock), .clr(reset));
  Register #(.width(3)) vx (.D(multiplexer_4_out), .en(or_3_out), .Q(vxy[2:0]), .clk(clock));  // open: clr
  Multiplexer #(.width(8)) multiplexer_5 (.in0(scA_q), .in1(adder_5_out), .out(scoreA), .sel(hitB));  // open: en
  Adder adder_5 (.a(scA_q), .b(8'h1), .out(adder_5_out));  // open: cin, cout
  reflect reflect_2 (.\input (vxy[5:3]), .\output (reflect_2_output));
  Multiplexer #(.width(3)) multiplexer_6 (
    .in0(reflect_2_output), .in1(3'b001), .out(multiplexer_6_out), .sel(reset));  // open: en
  or or_4 (or_4_out, reset, yrefl);
  Register #(.width(3)) vy (.D(multiplexer_6_out), .en(or_4_out), .Q(vxy[5:3]), .clk(clock));  // open: clr
  Register scB (.D(scoreB), .en(hitA), .Q(scB_q), .clk(clock), .clr(reset));
  Adder adder_6 (.a(scB_q), .b(8'h1), .out(adder_6_out));  // open: cin, cout
  Multiplexer #(.width(8)) multiplexer_7 (.in0(scB_q), .in1(adder_6_out), .out(scoreB), .sel(hitA));  // open: en
  and and_3 (hitA, xrefl, vxy[2]);
  Adder adder_7 (.a({ballX, xball[2:0]}), .b(8'h1c), .out(adder_7_out));  // open: cin, cout
  and and_4 (hitB, xrefl, not_6_out);
  not not_6 (not_6_out, vxy[2]);
  Adder adder_8 (.a({{6{vxy[2]}}, vxy[1:0]}), .b({ballX, xball[2:0]}), .cout(adder_8_cout));  // open: out, cin
  Comparator #(.width(1)) comparator_2 (.a(adder_8_cout), .b(vxy[2]), .eq(comparator_2_eq));  // open: gt, lt
  Adder adder_9 (.a({{6{vxy[5]}}, vxy[4:3]}), .b({ballY, yball[2:0]}), .cout(adder_9_cout));  // open: out, cin
  not not_7 (yrefl, comparator_3_eq);
  Comparator #(.width(1)) comparator_3 (.a(adder_9_cout), .b(vxy[5]), .eq(comparator_3_eq));  // open: gt, lt
  Adder adder_10 (.a(adder_7_out), .b({{6{vxy[2]}}, vxy[1:0]}), .cout(adder_10_cout));  // open: out, cin
  Comparator #(.width(1)) comparator_4 (.a(adder_10_cout), .b(vxy[2]), .eq(comparator_4_eq));  // open: gt, lt
  inrange inrange_2 (.Yball(ballY), .Ybat(rightYout), .ShowArow(inrange_2_showarow));
  not not_8 (xrefl, comparator_2_eq);
  not not_9 (not_9_out, comparator_4_eq);
  and and_5 (RBcontact, not_9_out, inrange_2_showarow);
  or or_5 (Bcontact, RBcontact, LBcontact);

  assign chipId = {5{1'b0}};
  assign leftYout = leftYIn;
  assign vxy[7:6] = 2'b00;
  assign xball[7:3] = ballX;
  assign yball[7:3] = ballY;

  // Other names for the same wires on the sheet: xreg[7:0] = {ballX, xball[2:0]}; yreg[7:0] = {ballY, yball[2:0]};
  //   longVX[7:0] = {{6{vxy[2]}}, vxy[1:0]}; vx[2:0] = vxy[2:0]; vxneg = vxy[2];
  //   longVY[7:0] = {{6{vxy[5]}}, vxy[4:3]}; vy[2:0] = vxy[5:3]; vyneg = vxy[5]; ScA[7:0] = scoreA; ScB[7:0] = scoreB
endmodule

module \program  (
  input  [7:0] vxy,
  input  [7:0] xball,
  input  [7:0] yball
);
endmodule
